# Fritzing sketch Ceng318Design (saved by Fritzing 0.9.3b)
circuit board: 9.31496cm x 5.38627cm
breadboards: 1

parts:
  Willwin_MQ-2 = MQ-4
  STM32Duino_Blue_Pill = BluePill

nets:
  VCC: Willwin_MQ-2.VCC, STM32Duino_Blue_Pill.3V3
  GND: Willwin_MQ-2.GND, STM32Duino_Blue_Pill.GND
  N1: Willwin_MQ-2.DO, STM32Duino_Blue_Pill.B8
  N2: Willwin_MQ-2.AO, STM32Duino_Blue_Pill.A1

notes:
  Smart Home Monitor
  Lucas Finiello
